# Fritzing sketch 11 (saved by Fritzing 0.9.3b)
breadboards: 1

parts:
  R1 = Resistor [tolerance=±5% resistance=1k package=THT]
  R2 = Resistor [tolerance=±5% resistance=200 package=THT]
  R3 = Resistor [tolerance=±5% resistance=200 package=THT]
  R4 = Resistor [tolerance=±5% resistance=200 package=THT]
  R5 = Resistor [tolerance=±5% resistance=200 package=THT]
  R6 = Resistor [tolerance=±5% resistance=200 package=THT]
  R7 = Resistor [tolerance=±5% resistance=200 package=THT]
  Seven_Segment_Display = Header 6 [package=1x06-smd]
  JP2 = Header 6 [package=1x06-smd]
  R8 = Resistor [tolerance=±5% resistance=1k package=THT]

nets:
  Arduino GPIO6: R1.Pin_0
  N1: R1.Pin_1, Seven_Segment_Display.1
  Arduino GPIO7: R2.Pin_0
  N2: R2.Pin_1, Seven_Segment_Display.2
  Arduino GPIO8: R3.Pin_0
  N3: R3.Pin_1, Seven_Segment_Display.3
  Arduino GPIO10: R4.Pin_0
  N4: R4.Pin_1, Seven_Segment_Display.5
  Arduino GPIO9: R5.Pin_0
  N5: R5.Pin_1, Seven_Segment_Display.4
  Arduino GPIO13: R6.Pin_0
  N6: R6.Pin_1, JP2.5
  Arduino GPIO12: R7.Pin_0
  N7: R7.Pin_1, JP2.4
  Arduino GPIO2: Seven_Segment_Display.6
  N8: JP2.1, R8.Pin_1
  Arduino GPIO3: JP2.2
  Arduino GPIO4: JP2.3
  Arduino GPIO5: JP2.6
  Arduino GPIO11: R8.Pin_0

notes:
  D1
  D2
  D3
  D4
  DP
  A
  B
  D
  C
  E
  F
  G
