# Fritzing sketch 09 (saved by Fritzing 0.9.3b)
breadboards: 1

parts:
  DS18B20 = Header 3 [package=jst-3-pth]

nets:
  3.3V: DS18B20.1
  Expansion GPIO19: DS18B20.2
  GND: DS18B20.3

notes:
  VDD
  GND
  DQ
