# Fritzing sketch 10 (saved by Fritzing 0.9.3b)
breadboards: 1

parts:
  DS18B20 = Header 3 [package=jst-3-pth]
  LCD_Screen = Header 4 [package=molex-1x4_lock]

nets:
  3.3V: DS18B20.1, LCD_Screen.1
  Expansion GPIO19: DS18B20.2
  GND: DS18B20.3, LCD_Screen.4
  Expansion SDA: LCD_Screen.2
  Expansion SCL: LCD_Screen.3

notes:
  VDD
  GND
  DQ
  SCL
  SDA
  Vcc
